// Logisim project cpu.circ as structural Verilog
module _1bRegister (
  input  CLK,
  input  CLR,
  input  LOAD,
  input  S,
  output Q
);

  wire and_1_out, and_2_out, not_1_out, or_1_out;

  not not_1 (not_1_out, LOAD);
  and and_1 (and_1_out, Q, not_1_out);
  or or_1 (or_1_out, and_1_out, and_2_out);
  and and_2 (and_2_out, LOAD, S);
  DFlipFlop dflipflop_1 (.CLR(CLR), .CLK(CLK), .D(or_1_out), .Q(Q));  // open: PRE, NOT_Q
endmodule

module DFlipFlop (
  input  PRE,
  input  CLR,
  input  CLK,
  input  D,
  output Q,
  output NOT_Q
);

  wire nand_1_out, nand_2_out, nand_3_out, nand_4_out, not_1_out, not_2_out;

  not not_1 (not_1_out, PRE);
  not not_2 (not_2_out, CLR);
  nand nand_1 (nand_1_out, not_1_out, nand_4_out, nand_2_out);
  nand nand_2 (nand_2_out, nand_1_out, not_2_out, CLK);
  nand nand_3 (nand_3_out, nand_2_out, CLK, nand_4_out);
  nand nand_4 (nand_4_out, nand_3_out, not_2_out, D);
  nand nand_5 (Q, not_1_out, nand_2_out, NOT_Q);
  nand nand_6 (NOT_Q, Q, not_2_out, nand_3_out);
endmodule

module _4bRegister (
  input  A0,
  input  A1,
  input  A2,
  input  A3,
  input  CLR,
  input  LOAD,
  input  CLK,
  output S0,
  output S1,
  output S2,
  output S3
);

  _1bRegister u_1bregister_1 (.Q(S0), .LOAD(LOAD), .S(A0), .CLK(CLK), .CLR(CLR));
  _1bRegister u_1bregister_2 (.Q(S1), .LOAD(LOAD), .S(A1), .CLK(CLK), .CLR(CLR));
  _1bRegister u_1bregister_3 (.Q(S2), .LOAD(LOAD), .S(A2), .CLK(CLK), .CLR(CLR));
  _1bRegister u_1bregister_4 (.Q(S3), .LOAD(LOAD), .S(A3), .CLK(CLK), .CLR(CLR));
endmodule

module _4bBuffer (
  input  A0,
  input  A1,
  input  A2,
  input  A3,
  input  ENABLE,
  output S0,
  output S1,
  output S2,
  output S3
);

  assign S0 = ENABLE ? A0 : 1'bz;  // Controlled_Buffer controlled_buffer_1
  assign S1 = ENABLE ? A1 : 1'bz;  // Controlled_Buffer controlled_buffer_2
  assign S2 = ENABLE ? A2 : 1'bz;  // Controlled_Buffer controlled_buffer_3
  assign S3 = ENABLE ? A3 : 1'bz;  // Controlled_Buffer controlled_buffer_4
endmodule

module _4bBufferedReg (
  input  A0,
  input  A1,
  input  A2,
  input  A3,
  input  LOAD,
  input  CLR,
  input  CLK,
  input  ENABLE,
  output S0,
  output S1,
  output S2,
  output S3,
  output [3:0] A0_A4
);

  _4bRegister u_4bregister_1 (
    .S0(A0_A4[0]), .S1(A0_A4[1]), .S2(A0_A4[2]), .S3(A0_A4[3]), .CLR(CLR), .A0(A0), .A1(A1), .A2(A2),
    .A3(A3), .LOAD(LOAD), .CLK(CLK));
  _4bBuffer u_4bbuffer_1 (
    .S0(S0), .S1(S1), .S2(S2), .S3(S3), .A0(A0_A4[0]), .A1(A0_A4[1]), .A2(A0_A4[2]), .A3(A0_A4[3]),
    .ENABLE(ENABLE));
endmodule

module _8bBufferedReg (
  input  E,
  input  [7:0] DATA_IN,
  input  CLR,
  input  LOAD,
  input  CLK,
  output [7:0] A0_A7,
  output [7:0] BUS
);

  _4bBufferedReg u_4bbufferedreg_1 (
    .S0(BUS[0]), .S1(BUS[1]), .S2(BUS[2]), .S3(BUS[3]), .A0_A4(A0_A7[3:0]), .A0(DATA_IN[0]), .A1(DATA_IN[1]),
    .A2(DATA_IN[2]), .A3(DATA_IN[3]), .LOAD(LOAD), .CLR(CLR), .CLK(CLK), .ENABLE(E));
  _4bBufferedReg u_4bbufferedreg_2 (
    .S0(BUS[4]), .S1(BUS[5]), .S2(BUS[6]), .S3(BUS[7]), .A0_A4(A0_A7[7:4]), .A0(DATA_IN[4]), .A1(DATA_IN[5]),
    .A2(DATA_IN[6]), .A3(DATA_IN[7]), .LOAD(LOAD), .CLR(CLR), .CLK(CLK), .ENABLE(E));
endmodule

module _8bReg (
  input  A0,
  input  A1,
  input  A2,
  input  A3,
  input  A4,
  input  A5,
  input  A6,
  input  A7,
  input  LD,
  input  CLR,
  input  CLK,
  output S0,
  output S1,
  output S2,
  output S3,
  output S4,
  output S5,
  output S6,
  output S7
);

  _4bRegister u_4bregister_1 (
    .S0(S0), .S1(S1), .S2(S2), .S3(S3), .CLR(CLR), .A0(A0), .A1(A1), .A2(A2), .A3(A3), .LOAD(LD), .CLK(CLK));
  _4bRegister u_4bregister_2 (
    .S0(S4), .S1(S5), .S2(S6), .S3(S7), .CLR(CLR), .A0(A4), .A1(A5), .A2(A6), .A3(A7), .LOAD(LD), .CLK(CLK));
endmodule

module Instruction_Register (
  input  CLR,
  input  LD,
  input  CLK,
  input  [7:0] DATA_IN,
  input  IO,
  output [7:0] BUS,
  output [3:0] IR0_IR3,
  output [3:0] IR4_IR7
);

  wire pull_resistor_1_node;

  Pull_Resistor pull_resistor_1 (.node(pull_resistor_1_node));
  _8bBuffer u_8bbuffer_1 (
    .A0(IR0_IR3[0]), .A1(IR0_IR3[1]), .A2(IR0_IR3[2]), .A3(IR0_IR3[3]), .A4(pull_resistor_1_node),
    .A5(pull_resistor_1_node), .A6(pull_resistor_1_node), .A7(pull_resistor_1_node), .IO(IO), .S0(BUS[0]),
    .S1(BUS[1]), .S2(BUS[2]), .S3(BUS[3]), .S4(BUS[4]), .S5(BUS[5]), .S6(BUS[6]), .S7(BUS[7]));
  _8bReg u_8breg_1 (
    .S0(IR0_IR3[0]), .S1(IR0_IR3[1]), .S2(IR0_IR3[2]), .S3(IR0_IR3[3]), .S4(IR4_IR7[0]), .S5(IR4_IR7[1]),
    .S6(IR4_IR7[2]), .S7(IR4_IR7[3]), .A0(DATA_IN[0]), .A1(DATA_IN[1]), .A2(DATA_IN[2]), .A3(DATA_IN[3]),
    .A4(DATA_IN[4]), .A5(DATA_IN[5]), .A6(DATA_IN[6]), .A7(DATA_IN[7]), .LD(LD), .CLR(CLR), .CLK(CLK));
endmodule

module _8bBuffer (
  input  A0,
  input  A1,
  input  A2,
  input  A3,
  input  A4,
  input  A5,
  input  A6,
  input  A7,
  input  IO,
  output S0,
  output S1,
  output S2,
  output S3,
  output S4,
  output S5,
  output S6,
  output S7
);

  _4bBuffer u_4bbuffer_1 (.S0(S0), .S1(S1), .S2(S2), .S3(S3), .A0(A0), .A1(A1), .A2(A2), .A3(A3), .ENABLE(IO));
  _4bBuffer u_4bbuffer_2 (.S0(S4), .S1(S5), .S2(S6), .S3(S7), .A0(A4), .A1(A5), .A2(A6), .A3(A7), .ENABLE(IO));
endmodule

module _4bAdder (
  input  C_IN,
  input  A0,
  input  B0,
  input  A1,
  input  B1,
  input  A2,
  input  B2,
  input  A3,
  input  B3,
  output S0,
  output S1,
  output S2,
  output S3,
  output C_OUT
);

  wire n1badder_1_cout, n1badder_2_cout, n1badder_3_cout;

  _1bAdder u_1badder_1 (.A(A0), .B(B0), .Cin(C_IN), .S(S0), .Cout(n1badder_1_cout));
  _1bAdder u_1badder_2 (.A(A1), .B(B1), .Cin(n1badder_1_cout), .S(S1), .Cout(n1badder_2_cout));
  _1bAdder u_1badder_3 (.A(A2), .B(B2), .Cin(n1badder_2_cout), .S(S2), .Cout(n1badder_3_cout));
  _1bAdder u_1badder_4 (.A(A3), .B(B3), .Cin(n1badder_3_cout), .S(S3), .Cout(C_OUT));
endmodule

module _1bAdder (
  input  A,
  input  B,
  input  Cin,
  output S,
  output Cout
);

  wire and_1_out, and_2_out, xor_1_out;

  xor xor_1 (xor_1_out, A, B);
  xor xor_2 (S, xor_1_out, Cin);
  and and_1 (and_1_out, Cin, xor_1_out);
  or or_1 (Cout, and_1_out, and_2_out);
  and and_2 (and_2_out, B, A);
endmodule

module _8bAdder (
  input  B0,
  input  A0,
  input  A1,
  input  B1,
  input  A2,
  input  B2,
  input  A3,
  input  B3,
  input  ADD_SUB,
  input  B4,
  input  A4,
  input  A5,
  input  B5,
  input  A6,
  input  B6,
  input  A7,
  input  B7,
  output S0,
  output S1,
  output S2,
  output S3,
  output S4,
  output S5,
  output S6,
  output S7,
  output C_OUT
);

  wire n4badder_1_c_out, xor_1_out, xor_2_out, xor_3_out, xor_4_out, xor_5_out, xor_6_out, xor_7_out,
       xor_8_out;

  xor xor_1 (xor_1_out, B0, ADD_SUB);
  xor xor_2 (xor_2_out, B1, ADD_SUB);
  xor xor_3 (xor_3_out, B2, ADD_SUB);
  xor xor_4 (xor_4_out, B3, ADD_SUB);
  xor xor_5 (xor_5_out, B4, ADD_SUB);
  xor xor_6 (xor_6_out, B5, ADD_SUB);
  xor xor_7 (xor_7_out, B6, ADD_SUB);
  xor xor_8 (xor_8_out, B7, ADD_SUB);
  _4bAdder u_4badder_1 (
    .C_IN(ADD_SUB), .A0(A0), .B0(xor_1_out), .A1(A1), .B1(xor_2_out), .A2(A2), .B2(xor_3_out), .A3(A3),
    .B3(xor_4_out), .S0(S0), .S1(S1), .S2(S2), .S3(S3), .C_OUT(n4badder_1_c_out));
  _4bAdder u_4badder_2 (
    .C_IN(n4badder_1_c_out), .A0(A4), .B0(xor_5_out), .A1(A5), .B1(xor_6_out), .A2(A6), .B2(xor_7_out),
    .A3(A7), .B3(xor_8_out), .S0(S4), .S1(S5), .S2(S6), .S3(S7), .C_OUT(C_OUT));
endmodule

module ALU (
  input  EO,
  input  A0,
  input  B0,
  input  A1,
  input  B1,
  input  A2,
  input  B2,
  input  A3,
  input  B3,
  input  A4,
  input  B4,
  input  A5,
  input  B5,
  input  A6,
  input  B6,
  input  A7,
  input  B7,
  input  SUB,
  input  FI,
  input  FLG_CLR,
  input  CLK,
  output [7:0] BUS,
  output CF,
  output ZF
);

  wire n8badder_1_c_out, n8badder_1_s0, n8badder_1_s1, n8badder_1_s2, n8badder_1_s3, n8badder_1_s4,
       n8badder_1_s5, n8badder_1_s6, n8badder_1_s7, nor_1_out;

  _8bAdder u_8badder_1 (
    .S4(n8badder_1_s4), .S5(n8badder_1_s5), .S6(n8badder_1_s6), .S7(n8badder_1_s7), .C_OUT(n8badder_1_c_out),
    .S0(n8badder_1_s0), .S1(n8badder_1_s1), .S2(n8badder_1_s2), .S3(n8badder_1_s3), .ADD_SUB(SUB), .B0(B0),
    .B1(B1), .B2(B2), .B3(B3), .B4(B4), .B5(B5), .B6(B6), .B7(B7), .A0(A0), .A1(A1), .A2(A2), .A3(A3),
    .A4(A4), .A5(A5), .A6(A6), .A7(A7));
  _8bBuffer u_8bbuffer_1 (
    .A0(n8badder_1_s0), .A1(n8badder_1_s1), .A2(n8badder_1_s2), .A3(n8badder_1_s3), .A4(n8badder_1_s4),
    .A5(n8badder_1_s5), .A6(n8badder_1_s6), .A7(n8badder_1_s7), .IO(EO), .S0(BUS[0]), .S1(BUS[1]),
    .S2(BUS[2]), .S3(BUS[3]), .S4(BUS[4]), .S5(BUS[5]), .S6(BUS[6]), .S7(BUS[7]));
  nor nor_1 (nor_1_out, n8badder_1_s0, n8badder_1_s1, n8badder_1_s2, n8badder_1_s3, n8badder_1_s4, n8badder_1_s5, n8badder_1_s6, n8badder_1_s7);
  _4bRegister u_4bregister_1 (
    .S0(CF), .S1(ZF), .CLR(FLG_CLR), .A0(n8badder_1_c_out), .A1(nor_1_out), .LOAD(FI), .CLK(CLK));  // open: S2, S3, A2, A3
endmodule

module _4t16Decoder (
  input  E,
  input  A0,
  input  A1,
  input  A2,
  input  A3,
  output Q0,
  output Q1,
  output Q2,
  output Q3,
  output A4,
  output Q5,
  output Q6,
  output Q7,
  output Q8,
  output Q9,
  output Q10,
  output Q11,
  output Q12,
  output Q13,
  output Q14,
  output Q15
);

  wire n2t4decoder_1_d0, n2t4decoder_1_d1, n2t4decoder_1_d2, n2t4decoder_1_d3;

  _2t4Decoder u_2t4decoder_1 (
    .A0(A2), .E(E), .A1(A3), .D0(n2t4decoder_1_d0), .D1(n2t4decoder_1_d1), .D2(n2t4decoder_1_d2),
    .D3(n2t4decoder_1_d3));
  _2t4Decoder u_2t4decoder_2 (.A0(A0), .E(n2t4decoder_1_d0), .A1(A1), .D0(Q0), .D1(Q1), .D2(Q2), .D3(Q3));
  _2t4Decoder u_2t4decoder_3 (.A0(A0), .E(n2t4decoder_1_d1), .A1(A1), .D0(A4), .D1(Q5), .D2(Q6), .D3(Q7));
  _2t4Decoder u_2t4decoder_4 (.A0(A0), .E(n2t4decoder_1_d2), .A1(A1), .D0(Q8), .D1(Q9), .D2(Q10), .D3(Q11));
  _2t4Decoder u_2t4decoder_5 (.A0(A0), .E(n2t4decoder_1_d3), .A1(A1), .D0(Q12), .D1(Q13), .D2(Q14), .D3(Q15));
endmodule

module _2t4Decoder (
  input  A0,
  input  E,
  input  A1,
  output D0,
  output D1,
  output D2,
  output D3
);

  wire not_1_out, not_2_out;

  not not_1 (not_1_out, A0);
  not not_2 (not_2_out, A1);
  and and_1 (D0, not_1_out, E, not_2_out);
  and and_2 (D1, A0, E, not_2_out);
  and and_3 (D2, A1, E, not_1_out);
  and and_4 (D3, A0, E, A1);
endmodule

module _2t1Multiplexer (
  input  A0,
  input  B0,
  input  SEL,
  input  E,
  output OUT
);

  wire and_1_out, and_2_out, not_1_out;

  not not_1 (not_1_out, SEL);
  and and_1 (and_1_out, A0, not_1_out, E);
  and and_2 (and_2_out, B0, SEL, E);
  or or_1 (OUT, and_1_out, and_2_out);
endmodule

module _4b2t1Multiplexer (
  input  A0,
  input  B0,
  input  A1,
  input  B1,
  input  A2,
  input  B2,
  input  A3,
  input  B3,
  input  SEL,
  input  E,
  output S0,
  output S1,
  output S2,
  output S3
);

  _2t1Multiplexer u_2t1multiplexer_1 (.A0(A0), .B0(B0), .SEL(SEL), .E(E), .OUT(S0));
  _2t1Multiplexer u_2t1multiplexer_2 (.A0(A1), .B0(B1), .SEL(SEL), .E(E), .OUT(S1));
  _2t1Multiplexer u_2t1multiplexer_3 (.A0(A2), .B0(B2), .SEL(SEL), .E(E), .OUT(S2));
  _2t1Multiplexer u_2t1multiplexer_4 (.A0(A3), .B0(B3), .SEL(SEL), .E(E), .OUT(S3));
endmodule

module _4t1Multiplexer (
  input  E,
  input  A0,
  input  A1,
  input  A2,
  input  A3,
  input  B0,
  input  B1,
  input  B2,
  input  B3,
  input  C0,
  input  C1,
  input  C2,
  input  C3,
  input  D0,
  input  D1,
  input  D2,
  input  D3,
  input  S1,
  input  S0,
  output Q0,
  output Q1,
  output Q2,
  output Q3
);

  wire n4b2t1multiplexer_1_s0, n4b2t1multiplexer_1_s1, n4b2t1multiplexer_1_s2, n4b2t1multiplexer_1_s3,
       n4b2t1multiplexer_2_s0, n4b2t1multiplexer_2_s1, n4b2t1multiplexer_2_s2, n4b2t1multiplexer_2_s3;

  _4b2t1Multiplexer u_4b2t1multiplexer_1 (
    .A0(A0), .B0(B0), .A1(A1), .B1(B1), .A2(A2), .B2(B2), .A3(A3), .B3(B3), .SEL(S0), .E(E),
    .S0(n4b2t1multiplexer_1_s0), .S1(n4b2t1multiplexer_1_s1), .S2(n4b2t1multiplexer_1_s2),
    .S3(n4b2t1multiplexer_1_s3));
  _4b2t1Multiplexer u_4b2t1multiplexer_2 (
    .A0(C0), .B0(D0), .A1(C1), .B1(D1), .A2(C2), .B2(D2), .A3(C3), .B3(D3), .SEL(S0), .E(E),
    .S0(n4b2t1multiplexer_2_s0), .S1(n4b2t1multiplexer_2_s1), .S2(n4b2t1multiplexer_2_s2),
    .S3(n4b2t1multiplexer_2_s3));
  _4b2t1Multiplexer u_4b2t1multiplexer_3 (
    .A0(n4b2t1multiplexer_1_s0), .B0(n4b2t1multiplexer_2_s0), .A1(n4b2t1multiplexer_1_s1),
    .B1(n4b2t1multiplexer_2_s1), .A2(n4b2t1multiplexer_1_s2), .B2(n4b2t1multiplexer_2_s2),
    .A3(n4b2t1multiplexer_1_s3), .B3(n4b2t1multiplexer_2_s3), .SEL(S1), .E(E), .S0(Q0), .S1(Q1), .S2(Q2),
    .S3(Q3));
endmodule

module _16t1Multiplexer (
  input  D0,
  input  D16,
  input  D1,
  input  D17,
  input  D2,
  input  D18,
  input  D3,
  input  D19,
  input  D4,
  input  D20,
  input  D5,
  input  D21,
  input  D6,
  input  D22,
  input  D7,
  input  D23,
  input  D8,
  input  D24,
  input  D9,
  input  D25,
  input  D10,
  input  D26,
  input  D11,
  input  D27,
  input  D12,
  input  D28,
  input  D13,
  input  D29,
  input  D14,
  input  D30,
  input  D15,
  input  D31,
  input  D32,
  input  D48,
  input  D33,
  input  D49,
  input  D34,
  input  D50,
  input  D35,
  input  D51,
  input  D36,
  input  D52,
  input  D37,
  input  D53,
  input  D38,
  input  D54,
  input  D39,
  input  D55,
  input  D40,
  input  D56,
  input  D41,
  input  D57,
  input  D42,
  input  D58,
  input  D43,
  input  D59,
  input  D44,
  input  D60,
  input  D45,
  input  D61,
  input  D46,
  input  D62,
  input  D47,
  input  D63,
  input  E,
  input  A3,
  input  A2,
  input  A1,
  input  A0,
  output S0,
  output S1,
  output S2,
  output S3
);

  wire [3:0] n4t1multiplexer_1_q0, n4t1multiplexer_2_q0, n4t1multiplexer_3_q0, n4t1multiplexer_4_q0;

  _4t1Multiplexer u_4t1multiplexer_1 (
    .E(E), .A0(D0), .A1(D1), .A2(D2), .A3(D3), .B0(D4), .B1(D5), .B2(D6), .B3(D7), .C0(D8), .C1(D9),
    .C2(D10), .C3(D11), .D0(D12), .D1(D13), .D2(D14), .D3(D15), .S1(A1), .S0(A0),
    .Q0(n4t1multiplexer_1_q0[0]), .Q1(n4t1multiplexer_1_q0[1]), .Q2(n4t1multiplexer_1_q0[2]),
    .Q3(n4t1multiplexer_1_q0[3]));
  _4t1Multiplexer u_4t1multiplexer_2 (
    .E(E), .A0(D32), .A1(D33), .A2(D34), .A3(D35), .B0(D36), .B1(D37), .B2(D38), .B3(D39), .C0(D40),
    .C1(D41), .C2(D42), .C3(D43), .D0(D44), .D1(D45), .D2(D46), .D3(D47), .S1(A1), .S0(A0),
    .Q0(n4t1multiplexer_2_q0[0]), .Q1(n4t1multiplexer_2_q0[1]), .Q2(n4t1multiplexer_2_q0[2]),
    .Q3(n4t1multiplexer_2_q0[3]));
  _4t1Multiplexer u_4t1multiplexer_3 (
    .E(E), .A0(D16), .A1(D17), .A2(D18), .A3(D19), .B0(D20), .B1(D21), .B2(D22), .B3(D23), .C0(D24),
    .C1(D25), .C2(D26), .C3(D27), .D0(D28), .D1(D29), .D2(D30), .D3(D31), .S1(A1), .S0(A0),
    .Q0(n4t1multiplexer_3_q0[0]), .Q1(n4t1multiplexer_3_q0[1]), .Q2(n4t1multiplexer_3_q0[2]),
    .Q3(n4t1multiplexer_3_q0[3]));
  _4t1Multiplexer u_4t1multiplexer_4 (
    .E(E), .A0(D48), .A1(D49), .A2(D50), .A3(D51), .B0(D52), .B1(D53), .B2(D54), .B3(D55), .C0(D56),
    .C1(D57), .C2(D58), .C3(D59), .D0(D60), .D1(D61), .D2(D62), .D3(D63), .S1(A1), .S0(A0),
    .Q0(n4t1multiplexer_4_q0[0]), .Q1(n4t1multiplexer_4_q0[1]), .Q2(n4t1multiplexer_4_q0[2]),
    .Q3(n4t1multiplexer_4_q0[3]));
  _4t1Multiplexer u_4t1multiplexer_5 (
    .E(E), .A0(n4t1multiplexer_1_q0[0]), .A1(n4t1multiplexer_1_q0[1]), .A2(n4t1multiplexer_1_q0[2]),
    .A3(n4t1multiplexer_1_q0[3]), .B0(n4t1multiplexer_3_q0[0]), .B1(n4t1multiplexer_3_q0[1]),
    .B2(n4t1multiplexer_3_q0[2]), .B3(n4t1multiplexer_3_q0[3]), .C0(n4t1multiplexer_2_q0[0]),
    .C1(n4t1multiplexer_2_q0[1]), .C2(n4t1multiplexer_2_q0[2]), .C3(n4t1multiplexer_2_q0[3]),
    .D0(n4t1multiplexer_4_q0[0]), .D1(n4t1multiplexer_4_q0[1]), .D2(n4t1multiplexer_4_q0[2]),
    .D3(n4t1multiplexer_4_q0[3]), .S1(A3), .S0(A2), .Q0(S0), .Q1(S1), .Q2(S2), .Q3(S3));
endmodule

module _4bMemoryAddressRegister (
  input  PROG,
  input  [3:0] DATA_IN,
  input  [3:0] BUS,
  input  CLR,
  input  LD,
  input  CLK,
  output [3:0] A0_A4
);

  wire n4bbufferedreg_1_s0, n4bbufferedreg_1_s1, n4bbufferedreg_1_s2, n4bbufferedreg_1_s3,
       pull_resistor_1_node, pull_resistor_2_node;

  Pull_Resistor #(.pull(1)) pull_resistor_1 (.node(pull_resistor_1_node));
  _4bBufferedReg u_4bbufferedreg_1 (
    .S0(n4bbufferedreg_1_s0), .S1(n4bbufferedreg_1_s1), .S2(n4bbufferedreg_1_s2), .S3(n4bbufferedreg_1_s3),
    .A0(BUS[0]), .A1(BUS[1]), .A2(BUS[2]), .A3(BUS[3]), .LOAD(LD), .CLR(CLR), .CLK(CLK),
    .ENABLE(pull_resistor_1_node));  // open: A0_A4
  Pull_Resistor #(.pull(1)) pull_resistor_2 (.node(pull_resistor_2_node));
  _4b2t1Multiplexer u_4b2t1multiplexer_1 (
    .A0(n4bbufferedreg_1_s0), .B0(DATA_IN[0]), .A1(n4bbufferedreg_1_s1), .B1(DATA_IN[1]),
    .A2(n4bbufferedreg_1_s2), .B2(DATA_IN[2]), .A3(n4bbufferedreg_1_s3), .B3(DATA_IN[3]), .SEL(PROG),
    .E(pull_resistor_2_node), .S0(A0_A4[0]), .S1(A0_A4[1]), .S2(A0_A4[2]), .S3(A0_A4[3]));
endmodule

module _16x4bRAM (
  input  WRITE_E,
  input  CLR,
  input  D0,
  input  D1,
  input  D2,
  input  D3,
  input  A0,
  input  A1,
  input  A2,
  input  A3,
  output S0,
  output S1,
  output S2,
  output S3
);

  wire n4t16decoder_1_a4, n4t16decoder_1_q0, n4t16decoder_1_q1, n4t16decoder_1_q2, n4t16decoder_1_q3,
       n4t16decoder_1_q5, n4t16decoder_1_q6, n4t16decoder_1_q7, n4t16decoder_1_q8, n4t16decoder_1_q9,
       n4t16decoder_1_q10, n4t16decoder_1_q11, n4t16decoder_1_q12, n4t16decoder_1_q13, n4t16decoder_1_q14,
       n4t16decoder_1_q15, not_1_out;
  wire [3:0] n4bregister_1_s0, n4bregister_2_s0, n4bregister_3_s0, n4bregister_4_s0, n4bregister_5_s0,
       n4bregister_6_s0, n4bregister_7_s0, n4bregister_8_s0, n4bregister_9_s0, n4bregister_10_s0,
       n4bregister_11_s0, n4bregister_12_s0, n4bregister_13_s0, n4bregister_14_s0, n4bregister_15_s0,
       n4bregister_16_s0;

  _4t16Decoder u_4t16decoder_1 (
    .Q0(n4t16decoder_1_q0), .Q1(n4t16decoder_1_q1), .Q2(n4t16decoder_1_q2), .Q3(n4t16decoder_1_q3),
    .A4(n4t16decoder_1_a4), .Q5(n4t16decoder_1_q5), .Q6(n4t16decoder_1_q6), .Q7(n4t16decoder_1_q7),
    .Q8(n4t16decoder_1_q8), .Q9(n4t16decoder_1_q9), .Q10(n4t16decoder_1_q10), .Q11(n4t16decoder_1_q11),
    .Q12(n4t16decoder_1_q12), .Q13(n4t16decoder_1_q13), .Q14(n4t16decoder_1_q14), .Q15(n4t16decoder_1_q15),
    .A0(A0), .A1(A1), .A2(A2), .A3(A3), .E(WRITE_E));
  not not_1 (not_1_out, WRITE_E);
  _4bRegister u_4bregister_1 (
    .S0(n4bregister_1_s0[0]), .S1(n4bregister_1_s0[1]), .S2(n4bregister_1_s0[2]), .S3(n4bregister_1_s0[3]),
    .CLR(CLR), .A0(D0), .A1(D1), .A2(D2), .A3(D3), .LOAD(WRITE_E), .CLK(n4t16decoder_1_q0));
  _4bRegister u_4bregister_2 (
    .S0(n4bregister_2_s0[0]), .S1(n4bregister_2_s0[1]), .S2(n4bregister_2_s0[2]), .S3(n4bregister_2_s0[3]),
    .CLR(CLR), .A0(D0), .A1(D1), .A2(D2), .A3(D3), .LOAD(WRITE_E), .CLK(n4t16decoder_1_q2));
  _4bRegister u_4bregister_3 (
    .S0(n4bregister_3_s0[0]), .S1(n4bregister_3_s0[1]), .S2(n4bregister_3_s0[2]), .S3(n4bregister_3_s0[3]),
    .CLR(CLR), .A0(D0), .A1(D1), .A2(D2), .A3(D3), .LOAD(WRITE_E), .CLK(n4t16decoder_1_a4));
  _4bRegister u_4bregister_4 (
    .S0(n4bregister_4_s0[0]), .S1(n4bregister_4_s0[1]), .S2(n4bregister_4_s0[2]), .S3(n4bregister_4_s0[3]),
    .CLR(CLR), .A0(D0), .A1(D1), .A2(D2), .A3(D3), .LOAD(WRITE_E), .CLK(n4t16decoder_1_q6));
  _4bRegister u_4bregister_5 (
    .S0(n4bregister_5_s0[0]), .S1(n4bregister_5_s0[1]), .S2(n4bregister_5_s0[2]), .S3(n4bregister_5_s0[3]),
    .CLR(CLR), .A0(D0), .A1(D1), .A2(D2), .A3(D3), .LOAD(WRITE_E), .CLK(n4t16decoder_1_q1));
  _4bRegister u_4bregister_6 (
    .S0(n4bregister_6_s0[0]), .S1(n4bregister_6_s0[1]), .S2(n4bregister_6_s0[2]), .S3(n4bregister_6_s0[3]),
    .CLR(CLR), .A0(D0), .A1(D1), .A2(D2), .A3(D3), .LOAD(WRITE_E), .CLK(n4t16decoder_1_q3));
  _4bRegister u_4bregister_7 (
    .S0(n4bregister_7_s0[0]), .S1(n4bregister_7_s0[1]), .S2(n4bregister_7_s0[2]), .S3(n4bregister_7_s0[3]),
    .CLR(CLR), .A0(D0), .A1(D1), .A2(D2), .A3(D3), .LOAD(WRITE_E), .CLK(n4t16decoder_1_q5));
  _4bRegister u_4bregister_8 (
    .S0(n4bregister_8_s0[0]), .S1(n4bregister_8_s0[1]), .S2(n4bregister_8_s0[2]), .S3(n4bregister_8_s0[3]),
    .CLR(CLR), .A0(D0), .A1(D1), .A2(D2), .A3(D3), .LOAD(WRITE_E), .CLK(n4t16decoder_1_q7));
  _4bRegister u_4bregister_9 (
    .S0(n4bregister_9_s0[0]), .S1(n4bregister_9_s0[1]), .S2(n4bregister_9_s0[2]), .S3(n4bregister_9_s0[3]),
    .CLR(CLR), .A0(D0), .A1(D1), .A2(D2), .A3(D3), .LOAD(WRITE_E), .CLK(n4t16decoder_1_q8));
  _4bRegister u_4bregister_10 (
    .S0(n4bregister_10_s0[0]), .S1(n4bregister_10_s0[1]), .S2(n4bregister_10_s0[2]),
    .S3(n4bregister_10_s0[3]), .CLR(CLR), .A0(D0), .A1(D1), .A2(D2), .A3(D3), .LOAD(WRITE_E),
    .CLK(n4t16decoder_1_q10));
  _4bRegister u_4bregister_11 (
    .S0(n4bregister_11_s0[0]), .S1(n4bregister_11_s0[1]), .S2(n4bregister_11_s0[2]),
    .S3(n4bregister_11_s0[3]), .CLR(CLR), .A0(D0), .A1(D1), .A2(D2), .A3(D3), .LOAD(WRITE_E),
    .CLK(n4t16decoder_1_q12));
  _4bRegister u_4bregister_12 (
    .S0(n4bregister_12_s0[0]), .S1(n4bregister_12_s0[1]), .S2(n4bregister_12_s0[2]),
    .S3(n4bregister_12_s0[3]), .CLR(CLR), .A0(D0), .A1(D1), .A2(D2), .A3(D3), .LOAD(WRITE_E),
    .CLK(n4t16decoder_1_q14));
  _4bRegister u_4bregister_13 (
    .S0(n4bregister_13_s0[0]), .S1(n4bregister_13_s0[1]), .S2(n4bregister_13_s0[2]),
    .S3(n4bregister_13_s0[3]), .CLR(CLR), .A0(D0), .A1(D1), .A2(D2), .A3(D3), .LOAD(WRITE_E),
    .CLK(n4t16decoder_1_q9));
  _4bRegister u_4bregister_14 (
    .S0(n4bregister_14_s0[0]), .S1(n4bregister_14_s0[1]), .S2(n4bregister_14_s0[2]),
    .S3(n4bregister_14_s0[3]), .CLR(CLR), .A0(D0), .A1(D1), .A2(D2), .A3(D3), .LOAD(WRITE_E),
    .CLK(n4t16decoder_1_q11));
  _4bRegister u_4bregister_15 (
    .S0(n4bregister_15_s0[0]), .S1(n4bregister_15_s0[1]), .S2(n4bregister_15_s0[2]),
    .S3(n4bregister_15_s0[3]), .CLR(CLR), .A0(D0), .A1(D1), .A2(D2), .A3(D3), .LOAD(WRITE_E),
    .CLK(n4t16decoder_1_q13));
  _4bRegister u_4bregister_16 (
    .S0(n4bregister_16_s0[0]), .S1(n4bregister_16_s0[1]), .S2(n4bregister_16_s0[2]),
    .S3(n4bregister_16_s0[3]), .CLR(CLR), .A0(D0), .A1(D1), .A2(D2), .A3(D3), .LOAD(WRITE_E),
    .CLK(n4t16decoder_1_q15));
  _16t1Multiplexer u_16t1multiplexer_1 (
    .S0(S0), .S1(S1), .S2(S2), .S3(S3), .D0(n4bregister_1_s0[0]), .D1(n4bregister_1_s0[1]),
    .D2(n4bregister_1_s0[2]), .D3(n4bregister_1_s0[3]), .D4(n4bregister_5_s0[0]), .D5(n4bregister_5_s0[1]),
    .D6(n4bregister_5_s0[2]), .D7(n4bregister_5_s0[3]), .D8(n4bregister_2_s0[0]), .D9(n4bregister_2_s0[1]),
    .D10(n4bregister_2_s0[2]), .D11(n4bregister_2_s0[3]), .D12(n4bregister_6_s0[0]),
    .D13(n4bregister_6_s0[1]), .D14(n4bregister_6_s0[2]), .D15(n4bregister_6_s0[3]),
    .D32(n4bregister_9_s0[0]), .D33(n4bregister_9_s0[1]), .D34(n4bregister_9_s0[2]),
    .D35(n4bregister_9_s0[3]), .D36(n4bregister_13_s0[0]), .D37(n4bregister_13_s0[1]),
    .D38(n4bregister_13_s0[2]), .D39(n4bregister_13_s0[3]), .D40(n4bregister_10_s0[0]),
    .D41(n4bregister_10_s0[1]), .D42(n4bregister_10_s0[2]), .D43(n4bregister_10_s0[3]),
    .D44(n4bregister_14_s0[0]), .D45(n4bregister_14_s0[1]), .D46(n4bregister_14_s0[2]),
    .D47(n4bregister_14_s0[3]), .E(not_1_out), .A3(A3), .A2(A2), .A1(A1), .A0(A0), .D16(n4bregister_3_s0[0]),
    .D17(n4bregister_3_s0[1]), .D18(n4bregister_3_s0[2]), .D19(n4bregister_3_s0[3]),
    .D20(n4bregister_7_s0[0]), .D21(n4bregister_7_s0[1]), .D22(n4bregister_7_s0[2]),
    .D23(n4bregister_7_s0[3]), .D24(n4bregister_4_s0[0]), .D25(n4bregister_4_s0[1]),
    .D26(n4bregister_4_s0[2]), .D27(n4bregister_4_s0[3]), .D28(n4bregister_8_s0[0]),
    .D29(n4bregister_8_s0[1]), .D30(n4bregister_8_s0[2]), .D31(n4bregister_8_s0[3]),
    .D48(n4bregister_11_s0[0]), .D49(n4bregister_11_s0[1]), .D50(n4bregister_11_s0[2]),
    .D51(n4bregister_11_s0[3]), .D52(n4bregister_15_s0[0]), .D53(n4bregister_15_s0[1]),
    .D54(n4bregister_15_s0[2]), .D55(n4bregister_15_s0[3]), .D56(n4bregister_12_s0[0]),
    .D57(n4bregister_12_s0[1]), .D58(n4bregister_12_s0[2]), .D59(n4bregister_12_s0[3]),
    .D60(n4bregister_16_s0[0]), .D61(n4bregister_16_s0[1]), .D62(n4bregister_16_s0[2]),
    .D63(n4bregister_16_s0[3]));
endmodule

module RAM (
  input  A3,
  input  A2,
  input  A1,
  input  A0,
  input  CLR,
  input  TOGGLE,
  input  PROG,
  input  CLK,
  input  RI,
  input  RO,
  input  [7:0] DATA_IN,
  output [7:0] BUS,
  output [7:0] DATA
);

  wire n4b2t1multiplexer_1_p1, n4b2t1multiplexer_1_p2, n4b2t1multiplexer_1_p5;

  // _4b2t1Multiplexer 4b2t1multiplexer_1: pin names not known; wires that end beside it: n4b2t1multiplexer_1_p1, n4b2t1multiplexer_1_p2, TOGGLE, PROG, n4b2t1multiplexer_1_p5
  _16x4bRAM u_16x4bram_1 (
    .WRITE_E(n4b2t1multiplexer_1_p1), .CLR(CLR), .D0(DATA_IN[0]), .D1(DATA_IN[1]), .D2(DATA_IN[2]),
    .D3(DATA_IN[3]), .A0(A0), .A1(A1), .A2(A2), .A3(A3), .S0(DATA[0]), .S1(DATA[1]), .S2(DATA[2]),
    .S3(DATA[3]));
  and and_1 (n4b2t1multiplexer_1_p2, RI, CLK);
  Pull_Resistor #(.pull(1)) pull_resistor_1 (.node(n4b2t1multiplexer_1_p5));
  _16x4bRAM u_16x4bram_2 (
    .WRITE_E(n4b2t1multiplexer_1_p1), .CLR(CLR), .D0(DATA_IN[4]), .D1(DATA_IN[5]), .D2(DATA_IN[6]),
    .D3(DATA_IN[7]), .A0(A0), .A1(A1), .A2(A2), .A3(A3), .S0(DATA[4]), .S1(DATA[5]), .S2(DATA[6]),
    .S3(DATA[7]));
  _8bBuffer u_8bbuffer_1 (
    .A0(DATA[0]), .A1(DATA[1]), .A2(DATA[2]), .A3(DATA[3]), .A4(DATA[4]), .A5(DATA[5]), .A6(DATA[6]),
    .A7(DATA[7]), .IO(RO), .S0(BUS[0]), .S1(BUS[1]), .S2(BUS[2]), .S3(BUS[3]), .S4(BUS[4]), .S5(BUS[5]),
    .S6(BUS[6]), .S7(BUS[7]));
endmodule

module _4bSynCounter (
  input  INC,
  input  LD,
  input  CLR,
  input  CLK,
  input  D0,
  input  D1,
  input  D2,
  input  D3,
  output Q0,
  output Q1,
  output Q2,
  output Q3,
  output CARRY
);

  wire and_1_out, and_2_out, and_3_out, n4b2t1multiplexer_1_s0, n4b2t1multiplexer_1_s1,
       n4b2t1multiplexer_1_s2, n4b2t1multiplexer_1_s3, pull_resistor_1_node, xor_1_out, xor_2_out, xor_3_out,
       xor_4_out;

  xor xor_1 (xor_1_out, INC, Q0);
  Pull_Resistor #(.pull(1)) pull_resistor_1 (.node(pull_resistor_1_node));
  _4b2t1Multiplexer u_4b2t1multiplexer_1 (
    .A0(xor_4_out), .B0(D3), .A1(xor_3_out), .B1(D2), .A2(xor_2_out), .B2(D1), .A3(xor_1_out), .B3(D0),
    .SEL(LD), .E(pull_resistor_1_node), .S0(n4b2t1multiplexer_1_s0), .S1(n4b2t1multiplexer_1_s1),
    .S2(n4b2t1multiplexer_1_s2), .S3(n4b2t1multiplexer_1_s3));
  and and_1 (and_1_out, INC, Q0);
  DFlipFlop dflipflop_1 (.CLR(CLR), .CLK(CLK), .D(n4b2t1multiplexer_1_s3), .Q(Q0));  // open: PRE, NOT_Q
  xor xor_2 (xor_2_out, and_1_out, Q1);
  and and_2 (and_2_out, and_1_out, Q1);
  DFlipFlop dflipflop_2 (.CLR(CLR), .CLK(CLK), .D(n4b2t1multiplexer_1_s2), .Q(Q1));  // open: PRE, NOT_Q
  xor xor_3 (xor_3_out, and_2_out, Q2);
  and and_3 (and_3_out, and_2_out, Q2);
  DFlipFlop dflipflop_3 (.CLR(CLR), .CLK(CLK), .D(n4b2t1multiplexer_1_s1), .Q(Q2));  // open: PRE, NOT_Q
  xor xor_4 (xor_4_out, and_3_out, Q3);
  and and_4 (CARRY, and_3_out, Q3);
  DFlipFlop dflipflop_4 (.CLR(CLR), .CLK(CLK), .D(n4b2t1multiplexer_1_s0), .Q(Q3));  // open: PRE, NOT_Q
endmodule

module PC (
  input  CE,
  input  J,
  input  CLR,
  input  CLK,
  input  [3:0] DATA_IN,
  input  CO,
  output [3:0] PC_OUT,
  output [3:0] BUS_OUT
);

  _4bSynCounter u_4bsyncounter_1 (
    .INC(CE), .LD(J), .CLR(CLR), .CLK(CLK), .D0(DATA_IN[0]), .D1(DATA_IN[1]), .D2(DATA_IN[2]),
    .D3(DATA_IN[3]), .Q0(PC_OUT[0]), .Q1(PC_OUT[1]), .Q2(PC_OUT[2]), .Q3(PC_OUT[3]));  // open: CARRY
  _4bBuffer u_4bbuffer_1 (
    .S0(BUS_OUT[0]), .S1(BUS_OUT[1]), .S2(BUS_OUT[2]), .S3(BUS_OUT[3]), .A0(PC_OUT[0]), .A1(PC_OUT[1]),
    .A2(PC_OUT[2]), .A3(PC_OUT[3]), .ENABLE(CO));
endmodule

module SingleDigit7SDisplayDriver (
  input  [3:0] BCD_IN,
  output [6:0] SEG_OUT
);

  ROM #(.addrWidth(4), .dataWidth(7)) rom_1 (.addr(BCD_IN), .data(SEG_OUT));

  // Notes on the sheet:
  //   contents of rom_1 (hex, n*v repeats v):
  //   7e 30 6d 79 33 5b 5f 70 7f 7b
endmodule

module _3DigitBinaryToBCD (
  input  [7:0] BINARY_IN,
  output [3:0] BCD_0,
  output [3:0] BCD_1,
  output [3:0] BCD_2
);

  ROM #(.dataWidth(12)) rom_1 (.addr(BINARY_IN), .data({BCD_2, BCD_1, BCD_0}));

  // Notes on the sheet:
  //   contents of rom_1 (hex, n*v repeats v):
  //   0 1 2 3 4 5 6 7 8 9 10 11 12 13 14 15 16 17 18 19 20 21 22 23 24 25 26 27 28 29 30 31 32 33 34 35 36
  //   37 38 39 40 41 42 43 44 45 46 47 48 49 50 51 52 53 54 55 56 57 58 59 60 61 62 63 64 65 66 67 68 69
  //   70 71 72 73 74 75 76 77 78 79 80 81 82 83 84 85 86 87 88 89 90 91 92 93 94 95 96 97 98 99 100 101
  //   102 103 104 105 106 107 108 109 110 111 112 113 114 115 116 117 118 119 120 121 122 123 124 125 126
  //   127 128 129 130 131 132 133 134 135 136 137 138 139 140 141 142 143 144 145 146 147 148 149 150 151
  //   152 153 154 155 156 157 158 159 160 161 162 163 164 165 166 167 168 169 170 171 172 173 174 175 176
  //   177 178 179 180 181 182 183 184 185 186 187 188 189 190 191 192 193 194 195 196 197 198 199 200 201
  //   202 203 204 205 206 207 208 209 210 211 212 213 214 215 216 217 218 219 220 221 222 223 224 225 226
  //   227 228 229 230 231 232 233 234 235 236 237 238 239 240 241 242 243 244 245 246 247 248 249 250 251
  //   252 253 254 255
endmodule

module ControlLogic (
  input  CLR,
  input  CLK,
  input  [3:0] IR,
  input  CF,
  input  ZF,
  output FI,
  output J,
  output CO,
  output CE,
  output OI,
  output BI,
  output SU,
  output SO,
  output AO,
  output AI,
  output II,
  output IO,
  output RO,
  output RI,
  output MI,
  output HLT
);

  wire and_1_out, nor_1_out, nor_2_out, not_1_out, or_1_out, pull_resistor_1_node;
  wire [3:0] pc_1_pc_out, pull_resistor_5_node;

  not not_1 (not_1_out, CLK);
  Pull_Resistor #(.pull(1)) pull_resistor_1 (.node(pull_resistor_1_node));
  Pull_Resistor pull_resistor_2 (.node(pull_resistor_5_node[3]));
  Pull_Resistor pull_resistor_3 (.node(pull_resistor_5_node[2]));
  Pull_Resistor pull_resistor_4 (.node(pull_resistor_5_node[1]));
  Pull_Resistor pull_resistor_5 (.node(pull_resistor_5_node[0]));
  or or_1 (or_1_out, and_1_out, pc_1_pc_out[2]);
  PC pc_1 (
    .PC_OUT(pc_1_pc_out), .CE(pull_resistor_1_node), .J(or_1_out), .CLR(CLR), .CLK(not_1_out),
    .DATA_IN(pull_resistor_5_node));  // open: BUS_OUT, CO
  ROM #(.addrWidth(9), .dataWidth(16)) rom_1 (
    .addr({ZF, CF, IR, pc_1_pc_out[2:0]}),
    .data({HLT, MI, RI, RO, IO, II, AI, AO, SO, SU, BI, OI, CE, CO, J, FI}));
  nor nor_1 (nor_1_out, FI, J, CO, CE, OI, BI, SU, SO);
  nor nor_2 (nor_2_out, HLT, MI, RI, RO, IO, II, AI, AO);
  and and_1 (and_1_out, nor_1_out, nor_2_out);

  // Notes on the sheet:
  //   TODO: fix clear (now loading 0000)
  //   contents of rom_1 (hex, n*v repeats v):
  //   4004 1408 6*0 4004 1408 4800 1200 4*0 4004 1408 4800 1020 281 0 0 0 4004 1408 4800 1020 2c1 0 0 0
  //   4004 1408 4800 2100 4*0 4004 1408 a00 5*0 4004 1408 802 5*0 4004 1408 6*0 4004 1408 46*0 4004 1408
  //   110 5*0 8000 7*0 4004 1408 6*0 4004 1408 4800 1200 4*0 4004 1408 4800 1020 281 0 0 0 4004 1408 4800
  //   1020 2c1 0 0 0 4004 1408 4800 2100 4*0 4004 1408 a00 5*0 4004 1408 802 5*0 4004 1408 802 5*0 4004
  //   1408 46*0 4004 1408 110 5*0 8000 7*0 4004 1408 6*0 4004 1408 4800 1200 4*0 4004 1408 4800 1020 281 0
  //   0 0 4004 1408 4800 1020 2c1 0 0 0 4004 1408 4800 2100 4*0 4004 1408 a00 5*0 4004 1408 802 5*0 4004
  //   1408 6*0 4004 1408 802 45*0 4004 1408 110 5*0 8000 7*0 4004 1408 6*0 4004 1408 4800 1200 4*0 4004
  //   1408 4800 1020 281 0 0 0 4004 1408 4800 1020 2c1 0 0 0 4004 1408 4800 2100 4*0 4004 1408 a00 5*0
  //   4004 1408 802 5*0 4004 1408 802 5*0 4004 1408 802 45*0 4004 1408 110 5*0 8000
endmodule

module Clock (
  input  CLK_E,
  input  CLK,
  input  STEP,
  input  HLT,
  output OUT
);

  wire n2t1multiplexer_1_out, not_1_out, pull_resistor_1_node;

  Pull_Resistor #(.pull(1)) pull_resistor_1 (.node(pull_resistor_1_node));
  _2t1Multiplexer u_2t1multiplexer_1 (
    .A0(STEP), .B0(CLK), .SEL(CLK_E), .E(pull_resistor_1_node), .OUT(n2t1multiplexer_1_out));
  not not_1 (not_1_out, HLT);
  and and_1 (OUT, n2t1multiplexer_1_out, not_1_out);
endmodule

module RAM_Programmer (
  input  [7:0] DATA_IN,
  input  [3:0] ADDRESS,
  input  MANUAL,
  input  CLR,
  input  CLK,
  input  COMMIT,
  input  [7:0] BUS,
  input  PROG,
  output [7:0] RAM_DATA,
  output [3:0] RAM_ADD,
  output TOGGLE
);

  wire not_1_out, pull_resistor_1_node, pull_resistor_2_node, pull_resistor_3_node;
  wire [3:0] pc_1_pc_out;
  wire [7:0] controlled_buffer_1_out, n4b2t1multiplexer_1_s0, rom_1_data;

  Pull_Resistor #(.pull(1)) pull_resistor_1 (.node(pull_resistor_1_node));
  PC pc_1 (.PC_OUT(pc_1_pc_out), .CE(pull_resistor_1_node), .CLR(CLR), .CLK(CLK));  // open: BUS_OUT, J, DATA_IN, CO
  ROM #(.addrWidth(4)) rom_1 (.addr(pc_1_pc_out), .data(rom_1_data));
  not not_1 (not_1_out, CLK);
  Pull_Resistor #(.pull(1)) pull_resistor_2 (.node(pull_resistor_2_node));
  _4b2t1Multiplexer u_4b2t1multiplexer_1 (
    .A0(rom_1_data[0]), .B0(DATA_IN[0]), .A1(rom_1_data[1]), .B1(DATA_IN[1]), .A2(rom_1_data[2]),
    .B2(DATA_IN[2]), .A3(rom_1_data[3]), .B3(DATA_IN[3]), .SEL(MANUAL), .E(pull_resistor_2_node),
    .S0(n4b2t1multiplexer_1_s0[0]), .S1(n4b2t1multiplexer_1_s0[1]), .S2(n4b2t1multiplexer_1_s0[2]),
    .S3(n4b2t1multiplexer_1_s0[3]));
  _4b2t1Multiplexer u_4b2t1multiplexer_2 (
    .A0(rom_1_data[4]), .B0(DATA_IN[4]), .A1(rom_1_data[5]), .B1(DATA_IN[5]), .A2(rom_1_data[6]),
    .B2(DATA_IN[6]), .A3(rom_1_data[7]), .B3(DATA_IN[7]), .SEL(MANUAL), .E(pull_resistor_2_node),
    .S0(n4b2t1multiplexer_1_s0[4]), .S1(n4b2t1multiplexer_1_s0[5]), .S2(n4b2t1multiplexer_1_s0[6]),
    .S3(n4b2t1multiplexer_1_s0[7]));
  _4b2t1Multiplexer u_4b2t1multiplexer_3 (
    .A0(pc_1_pc_out[0]), .B0(ADDRESS[0]), .A1(pc_1_pc_out[1]), .B1(ADDRESS[1]), .A2(pc_1_pc_out[2]),
    .B2(ADDRESS[2]), .A3(pc_1_pc_out[3]), .B3(ADDRESS[3]), .SEL(MANUAL), .E(pull_resistor_2_node),
    .S0(RAM_ADD[0]), .S1(RAM_ADD[1]), .S2(RAM_ADD[2]), .S3(RAM_ADD[3]));
  _2t1Multiplexer u_2t1multiplexer_1 (
    .A0(not_1_out), .B0(COMMIT), .SEL(MANUAL), .E(pull_resistor_2_node), .OUT(TOGGLE));
  assign controlled_buffer_1_out = not_1_out ? n4b2t1multiplexer_1_s0 : 8'bz;  // Controlled_Buffer controlled_buffer_1
  Pull_Resistor #(.pull(1)) pull_resistor_3 (.node(pull_resistor_3_node));
  _4b2t1Multiplexer u_4b2t1multiplexer_4 (
    .A0(BUS[0]), .B0(controlled_buffer_1_out[0]), .A1(BUS[1]), .B1(controlled_buffer_1_out[1]), .A2(BUS[2]),
    .B2(controlled_buffer_1_out[2]), .A3(BUS[3]), .B3(controlled_buffer_1_out[3]), .SEL(PROG),
    .E(pull_resistor_3_node), .S0(RAM_DATA[0]), .S1(RAM_DATA[1]), .S2(RAM_DATA[2]), .S3(RAM_DATA[3]));
  _4b2t1Multiplexer u_4b2t1multiplexer_5 (
    .A0(BUS[4]), .B0(controlled_buffer_1_out[4]), .A1(BUS[5]), .B1(controlled_buffer_1_out[5]), .A2(BUS[6]),
    .B2(controlled_buffer_1_out[6]), .A3(BUS[7]), .B3(controlled_buffer_1_out[7]), .SEL(PROG),
    .E(pull_resistor_3_node), .S0(RAM_DATA[4]), .S1(RAM_DATA[5]), .S2(RAM_DATA[6]), .S3(RAM_DATA[7]));

  // Notes on the sheet:
  //   contents of rom_1 (hex, n*v repeats v):
  //   e0 2f 74 60 3f e0 80 64 f 6*0 a
endmodule

module CPU (
  input  CLK,
  input  CLR,
  input  PROG_RAM,
  input  MANUAL,
  input  [3:0] ADDRESS,
  input  [7:0] DATA_IN,
  output [7:0] A_DATA,
  output [3:0] MAR,
  output [7:0] BUS_DATA,
  output [7:0] RAM_DATA,
  output [3:0] IR_INS,
  output [3:0] IR_DATA,
  output [7:0] B_DATA,
  output [3:0] PC
);

  wire alu_1_cf, alu_1_zf, CLK_PROGRAMMER_out, clock_1_out, clock_2_out, COMMIT_out, controllogic_1_ai,
       controllogic_1_ao, controllogic_1_bi, controllogic_1_ce, controllogic_1_co, controllogic_1_fi,
       controllogic_1_hlt, controllogic_1_ii, controllogic_1_io, controllogic_1_j, controllogic_1_mi,
       controllogic_1_oi, controllogic_1_ri, controllogic_1_ro, controllogic_1_so, controllogic_1_su,
       ram_programmer_1_toggle, STEP_out;
  wire [3:0] n3digitbinarytobcd_1_bcd_0, n3digitbinarytobcd_1_bcd_1, n3digitbinarytobcd_1_bcd_2,
       ram_programmer_1_ram_add;
  wire [6:0] singledigit7sdisplaydriver_1_seg_out, singledigit7sdisplaydriver_2_seg_out,
       singledigit7sdisplaydriver_3_seg_out;
  wire [7:0] n8breg_1_s0, ram_programmer_1_ram_data;

  Clock_part CLK_PROGRAMMER (.out(CLK_PROGRAMMER_out));
  Button COMMIT (.out(COMMIT_out));
  _4bMemoryAddressRegister u_4bmemoryaddressregister_1 (
    .A0_A4(MAR), .BUS(BUS_DATA[3:0]), .CLR(CLR), .LD(controllogic_1_mi), .CLK(clock_2_out),
    .DATA_IN(ram_programmer_1_ram_add), .PROG(PROG_RAM));
  RAM ram_1 (
    .BUS(BUS_DATA), .DATA(RAM_DATA), .DATA_IN(ram_programmer_1_ram_data), .TOGGLE(ram_programmer_1_toggle),
    .A3(MAR[0]), .A2(MAR[1]), .A1(MAR[2]), .A0(MAR[3]), .CLR(CLR), .PROG(PROG_RAM), .CLK(clock_2_out),
    .RI(controllogic_1_ri), .RO(controllogic_1_ro));
  Instruction_Register instruction_register_1 (
    .BUS(BUS_DATA), .IR0_IR3(IR_DATA), .IR4_IR7(IR_INS), .IO(controllogic_1_io), .CLR(CLR),
    .LD(controllogic_1_ii), .CLK(clock_2_out), .DATA_IN(BUS_DATA));
  PC pc_1 (
    .PC_OUT(PC), .BUS_OUT(BUS_DATA[3:0]), .CE(controllogic_1_ce), .J(controllogic_1_j), .CLR(CLR),
    .CLK(clock_2_out), .DATA_IN(BUS_DATA[3:0]), .CO(controllogic_1_co));
  RAM_Programmer ram_programmer_1 (
    .RAM_DATA(ram_programmer_1_ram_data), .TOGGLE(ram_programmer_1_toggle),
    .RAM_ADD(ram_programmer_1_ram_add), .BUS(BUS_DATA), .PROG(PROG_RAM), .CLR(CLR), .CLK(CLK_PROGRAMMER_out),
    .ADDRESS(ADDRESS), .DATA_IN(DATA_IN), .MANUAL(MANUAL), .COMMIT(COMMIT_out));
  _7_Segment_Display u_7_segment_display_1 (
    .g(singledigit7sdisplaydriver_1_seg_out[0]), .f(singledigit7sdisplaydriver_1_seg_out[1]),
    .a(singledigit7sdisplaydriver_1_seg_out[6]), .b(singledigit7sdisplaydriver_1_seg_out[5]),
    .e(singledigit7sdisplaydriver_1_seg_out[2]), .d(singledigit7sdisplaydriver_1_seg_out[3]),
    .c(singledigit7sdisplaydriver_1_seg_out[4]));  // open: dp
  _7_Segment_Display u_7_segment_display_2 (
    .g(singledigit7sdisplaydriver_2_seg_out[0]), .f(singledigit7sdisplaydriver_2_seg_out[1]),
    .a(singledigit7sdisplaydriver_2_seg_out[6]), .b(singledigit7sdisplaydriver_2_seg_out[5]),
    .e(singledigit7sdisplaydriver_2_seg_out[2]), .d(singledigit7sdisplaydriver_2_seg_out[3]),
    .c(singledigit7sdisplaydriver_2_seg_out[4]));  // open: dp
  ControlLogic controllogic_1 (
    .CLR(CLR), .CLK(clock_2_out), .IR(IR_INS), .CF(alu_1_cf), .ZF(alu_1_zf), .FI(controllogic_1_fi),
    .J(controllogic_1_j), .CO(controllogic_1_co), .CE(controllogic_1_ce), .OI(controllogic_1_oi),
    .BI(controllogic_1_bi), .SU(controllogic_1_su), .SO(controllogic_1_so), .AO(controllogic_1_ao),
    .AI(controllogic_1_ai), .II(controllogic_1_ii), .IO(controllogic_1_io), .RO(controllogic_1_ro),
    .RI(controllogic_1_ri), .MI(controllogic_1_mi), .HLT(controllogic_1_hlt));
  Clock_part clock_1 (.out(clock_1_out));
  _7_Segment_Display u_7_segment_display_3 (
    .g(singledigit7sdisplaydriver_3_seg_out[0]), .f(singledigit7sdisplaydriver_3_seg_out[1]),
    .a(singledigit7sdisplaydriver_3_seg_out[6]), .b(singledigit7sdisplaydriver_3_seg_out[5]),
    .e(singledigit7sdisplaydriver_3_seg_out[2]), .d(singledigit7sdisplaydriver_3_seg_out[3]),
    .c(singledigit7sdisplaydriver_3_seg_out[4]));  // open: dp
  Button STEP (.out(STEP_out));
  Clock clock_2 (.OUT(clock_2_out), .CLK_E(CLK), .CLK(clock_1_out), .STEP(STEP_out), .HLT(controllogic_1_hlt));
  _8bBufferedReg REG_A (
    .A0_A7(A_DATA), .BUS(BUS_DATA), .DATA_IN(BUS_DATA), .CLR(CLR), .LOAD(controllogic_1_ai),
    .CLK(clock_2_out), .E(controllogic_1_ao));
  ALU alu_1 (
    .BUS(BUS_DATA), .CF(alu_1_cf), .ZF(alu_1_zf), .A0(A_DATA[0]), .B0(B_DATA[0]), .A1(A_DATA[1]),
    .B1(B_DATA[1]), .A2(A_DATA[2]), .B2(B_DATA[2]), .A3(A_DATA[3]), .B3(B_DATA[3]), .A4(A_DATA[4]),
    .B4(B_DATA[4]), .A5(A_DATA[5]), .B5(B_DATA[5]), .A6(A_DATA[6]), .B6(B_DATA[6]), .A7(A_DATA[7]),
    .B7(B_DATA[7]), .SUB(controllogic_1_su), .EO(controllogic_1_so), .FI(controllogic_1_fi), .FLG_CLR(CLR),
    .CLK(clock_2_out));
  _8bBufferedReg REG_B (
    .A0_A7(B_DATA), .BUS(BUS_DATA), .DATA_IN(BUS_DATA), .CLR(CLR), .LOAD(controllogic_1_bi), .CLK(clock_2_out));  // open: E
  _8bReg u_8breg_1 (
    .S0(n8breg_1_s0[0]), .S1(n8breg_1_s0[1]), .S2(n8breg_1_s0[2]), .S3(n8breg_1_s0[3]), .S4(n8breg_1_s0[4]),
    .S5(n8breg_1_s0[5]), .S6(n8breg_1_s0[6]), .S7(n8breg_1_s0[7]), .A0(BUS_DATA[0]), .A1(BUS_DATA[1]),
    .A2(BUS_DATA[2]), .A3(BUS_DATA[3]), .A4(BUS_DATA[4]), .A5(BUS_DATA[5]), .A6(BUS_DATA[6]),
    .A7(BUS_DATA[7]), .LD(controllogic_1_oi), .CLR(CLR), .CLK(clock_2_out));
  _3DigitBinaryToBCD u_3digitbinarytobcd_1 (
    .BINARY_IN(n8breg_1_s0), .BCD_0(n3digitbinarytobcd_1_bcd_0), .BCD_1(n3digitbinarytobcd_1_bcd_1),
    .BCD_2(n3digitbinarytobcd_1_bcd_2));
  SingleDigit7SDisplayDriver singledigit7sdisplaydriver_1 (
    .SEG_OUT(singledigit7sdisplaydriver_1_seg_out), .BCD_IN(n3digitbinarytobcd_1_bcd_2));
  SingleDigit7SDisplayDriver singledigit7sdisplaydriver_2 (
    .SEG_OUT(singledigit7sdisplaydriver_2_seg_out), .BCD_IN(n3digitbinarytobcd_1_bcd_1));
  SingleDigit7SDisplayDriver singledigit7sdisplaydriver_3 (
    .SEG_OUT(singledigit7sdisplaydriver_3_seg_out), .BCD_IN(n3digitbinarytobcd_1_bcd_0));
endmodule
